// Digital circuit better-logic.dig as structural Verilog
module better_logic (
  input  pxl
);

  wire _7405_1_pin6, _7405_2_pin8, _7411_1_pin5, _7411_1_pin6, _7411_1_pin12, _7411_2_pin5, _7411_2_pin6,
       _7411_2_pin12, _7411_3_pin5, _7411_3_pin6, _7411_3_pin8, _7411_3_pin11, _7411_4_pin6, _7411_4_pin8,
       _7411_5_pin8, CD4043B_nq, pullup_1_out, pullup_2_out, pullup_3_out, rs_ff_as_1_nq, rs_ff_as_3_q;
  wire [13:0] _7405_1_pin13, _7411_2_pin11;

  Break #(.Cycles(1000000)) vSync_set (.brk(_7411_3_pin6));
  Break #(.Cycles(1000000)) vSync_reset (.brk(_7411_4_pin6));
  Break #(.Cycles(1000000)) hSync_reset (.brk(_7411_1_pin6));
  PullUp pullup_1 (.out(pullup_1_out));
  PullUp pullup_2 (.out(pullup_2_out));
  PullUp pullup_3 (.out(pullup_3_out));
  Break #(.Cycles(1000000)) line_end (.brk(_7411_2_pin12));
  Break #(.Cycles(1000000)) frame_end (.brk(_7411_2_pin6));
  _7405 _7405_1 (
    .pin1(_7405_1_pin13[6]), .pin2(pullup_1_out), .pin3(_7405_1_pin13[5]), .pin4(pullup_1_out),
    .pin5(_7405_1_pin13[3]), .pin6(_7405_1_pin6), .pin7(1'b0), .pin8(_7405_1_pin6), .pin9(_7405_1_pin13[2]),
    .pin10(_7405_1_pin6), .pin11(_7405_1_pin13[1]), .pin12(_7405_1_pin6), .pin13(_7405_1_pin13[0]),
    .pin14(1'b1));
  _7411 _7411_1 (
    .pin1(_7405_1_pin6), .pin2(pullup_1_out), .pin3(_7405_1_pin13[5]), .pin4(_7405_1_pin13[6]),
    .pin5(_7411_1_pin5), .pin6(_7411_1_pin6), .pin7(1'b0), .pin8(_7411_1_pin5), .pin9(_7405_1_pin13[9]),
    .pin10(_7405_1_pin13[7]), .pin11(_7405_1_pin13[4]), .pin12(_7411_1_pin12), .pin13(_7411_1_pin5),
    .pin14(1'b1));
  Counter #(.Bits(14)) hCount__74HC4060 (.en(1'b1), .C(pxl), .clr(_7411_2_pin12), .out(_7405_1_pin13));  // open: ovf
  _7411 _7411_2 (
    .pin1(_7405_1_pin13[8]), .pin2(_7405_1_pin13[9]), .pin3(1'b1), .pin4(_7411_2_pin11[9]),
    .pin5(_7411_2_pin5), .pin6(_7411_2_pin6), .pin7(1'b0), .pin8(_7411_2_pin5), .pin9(_7411_2_pin11[3]),
    .pin10(_7411_2_pin11[2]), .pin11(_7411_2_pin11[0]), .pin12(_7411_2_pin12), .pin13(_7405_1_pin13[5]),
    .pin14(1'b1));
  Counter #(.Bits(14)) vCount__74HC4060 (
    .en(1'b1), .C(_7411_2_pin12), .clr(_7411_2_pin6), .out(_7411_2_pin11));  // open: ovf
  RS_FF_AS CD4043B (.S(_7411_1_pin12), .R(_7411_1_pin6), .nQ(CD4043B_nq));  // open: Q
  RS_FF_AS rs_ff_as_1 (.S(_7411_3_pin6), .R(_7411_4_pin6), .nQ(rs_ff_as_1_nq));  // open: Q
  RS_FF_AS rs_ff_as_2 (.S(1'b0), .R(1'b0));  // open: Q, nQ
  RS_FF_AS rs_ff_as_3 (.S(_7411_2_pin6), .R(_7411_5_pin8), .Q(rs_ff_as_3_q));  // open: nQ
  _7405 _7405_2 (
    .pin1(_7411_2_pin11[1]), .pin2(pullup_2_out), .pin3(_7411_2_pin11[2]), .pin4(pullup_3_out), .pin5(1'b0),
    .pin7(1'b0), .pin8(_7405_2_pin8), .pin9(_7411_2_pin11[0]), .pin10(_7405_2_pin8),
    .pin11(_7411_2_pin11[4]), .pin12(_7405_2_pin8), .pin13(_7411_2_pin11[9]), .pin14(1'b1));  // open: pin6
  _7411 _7411_3 (
    .pin1(_7411_2_pin11[8]), .pin2(_7405_2_pin8), .pin3(pullup_3_out), .pin4(_7411_2_pin11[1]),
    .pin5(_7411_3_pin5), .pin6(_7411_3_pin6), .pin7(1'b0), .pin8(_7411_3_pin8), .pin9(_7411_2_pin11[5]),
    .pin10(_7411_2_pin11[6]), .pin11(_7411_3_pin11), .pin12(_7411_3_pin11), .pin13(_7411_2_pin11[7]),
    .pin14(1'b1));
  _7411 _7411_4 (
    .pin1(_7411_3_pin8), .pin2(1'b1), .pin3(_7411_3_pin5), .pin4(pullup_2_out), .pin5(_7411_2_pin11[2]),
    .pin6(_7411_4_pin6), .pin7(1'b0), .pin8(_7411_4_pin8), .pin9(_7411_2_pin11[5]), .pin10(_7411_2_pin11[6]),
    .pin11(_7411_2_pin11[7]), .pin12(_7411_3_pin5), .pin13(_7411_2_pin11[3]), .pin14(1'b1));
  _7411 _7411_5 (
    .pin1(1'b0), .pin2(1'b0), .pin3(1'b0), .pin4(1'b0), .pin5(1'b0), .pin7(1'b0), .pin8(_7411_5_pin8),
    .pin9(1'b1), .pin10(_7411_2_pin11[8]), .pin11(_7411_4_pin8), .pin13(1'b1), .pin14(1'b1));  // open: pin6, pin12
  PullUp pullup_4 (.out(_7405_1_pin6));
  PullUp pullup_5 (.out(_7405_2_pin8));
  Break #(.Cycles(1000000)) vVis_reset (.brk(_7411_5_pin8));
  Break #(.Cycles(1000000)) hSync_set (.brk(_7411_1_pin12));
  VGA vga_1 (.R(1'b1), .G(1'b1), .B(1'b1), .H(CD4043B_nq), .V(rs_ff_as_1_nq), .C(pxl));

  // Notes on the sheet:
  //   pxl: Hz: 2147483647
  //   vVis
endmodule
