// Digital circuit signal generator and character indexer.dig as structural Verilog
module signal_generator_and_character_indexer (
  input  pxl
);

  wire _7404_1_pin3, _7404_1_pin4, _7404_1_pin5, _7404_1_pin6, _7404_2_pin9, _7404_3_pin10, _7404_3_pin11,
       _7404_3_pin12, _7408_1_pin8, _7408_1_pin10, _7408_1_pin12, _7411_1_pin1, _7411_1_pin4, _7411_1_pin5,
       _7411_1_pin6, _7411_1_pin8, _7411_1_pin10, _7411_1_pin12, _7421_1_pin4, _7421_1_pin5, _7421_1_pin9,
       _7421_1_pin10, _7421_1_pin12, _7421_1_pin13, _7421_2_pin8, _7421_2_pin9, _7421_2_pin10, _7421_2_pin12,
       _7421_3_pin8, _7432_1_pin4, _7432_1_pin5, _7432_1_pin6, _7432_1_pin8, _7432_1_pin10, _7455_1_pin2,
       _7455_1_pin3, _7455_1_pin4, _7455_1_pin8, _7455_1_pin12, _7458_1_pin1, _7458_1_pin4, _7458_1_pin8,
       _74161_1_pin1, _74161_1_pin11, _74161_1_pin12, _74161_1_pin13, _74161_1_pin14, _74161_2_pin11,
       _74161_2_pin12, _74161_2_pin13, _74161_2_pin14, _74161_2_pin15, _74161_3_pin14, _74161_4_pin13,
       _74161_4_pin15, _74161_5_pin11, _74161_5_pin12, _74161_5_pin13, _74161_5_pin14, _74161_5_pin15,
       _74161_6_pin14, _74808_1_p13, _74808_1_p16, not_2_out, not_3_out, or_1_out, or_2_out;

  _74161 _74161_1 (
    .pin1(_74161_1_pin1), .pin2(pxl), .pin3(1'b0), .pin4(1'b0), .pin5(1'b0), .pin6(1'b0), .pin7(1'b1),
    .pin8(1'b0), .pin9(1'b1), .pin10(1'b1), .pin11(_74161_1_pin11), .pin12(_74161_1_pin12),
    .pin13(_74161_1_pin13), .pin14(_74161_1_pin14), .pin16(1'b1));  // open: pin15
  _7404 _7404_1 (
    .pin1(_74161_1_pin11), .pin2(_74161_1_pin1), .pin3(_7404_1_pin3), .pin4(_7404_1_pin4),
    .pin5(_7404_1_pin5), .pin6(_7404_1_pin6), .pin7(1'b0), .pin9(1'b0), .pin11(1'b0), .pin13(1'b0),
    .pin14(1'b1));  // open: pin8, pin10, pin12
  _74161 _74161_2 (
    .pin1(_7404_1_pin6), .pin2(_74161_1_pin11), .pin3(1'b0), .pin4(1'b0), .pin5(1'b0), .pin6(1'b0),
    .pin7(1'b1), .pin8(1'b0), .pin9(1'b1), .pin10(1'b1), .pin11(_74161_2_pin11), .pin12(_74161_2_pin12),
    .pin13(_74161_2_pin13), .pin14(_74161_2_pin14), .pin15(_74161_2_pin15), .pin16(1'b1));
  _7421 _7421_1 (
    .pin1(_74161_2_pin12), .pin2(1'b1), .pin4(_7421_1_pin4), .pin5(_7421_1_pin5), .pin6(_7404_1_pin5),
    .pin7(1'b0), .pin8(_7404_1_pin3), .pin9(_7421_1_pin9), .pin10(_7421_1_pin10), .pin12(_7421_1_pin12),
    .pin13(_7421_1_pin13), .pin14(1'b1));  // open: pin3, pin11
  _74161 _74161_3 (
    .pin1(_7404_1_pin6), .pin2(_74161_1_pin11), .pin3(1'b0), .pin4(1'b0), .pin5(1'b0), .pin6(1'b0),
    .pin7(1'b1), .pin8(1'b0), .pin9(1'b1), .pin10(_74161_2_pin15), .pin12(_7421_1_pin4),
    .pin13(_7421_1_pin5), .pin14(_74161_3_pin14), .pin16(1'b1));  // open: pin11, pin15
  _74161 _74161_4 (
    .pin1(_7404_1_pin4), .pin2(_7404_1_pin6), .pin3(1'b0), .pin4(1'b0), .pin5(1'b0), .pin6(1'b0),
    .pin7(1'b1), .pin8(1'b0), .pin9(1'b1), .pin10(1'b1), .pin11(_7421_1_pin12), .pin12(_7421_1_pin10),
    .pin13(_74161_4_pin13), .pin14(_7421_1_pin9), .pin15(_74161_4_pin15), .pin16(1'b1));
  _74161 _74161_5 (
    .pin1(_7404_1_pin4), .pin2(_7404_1_pin6), .pin3(1'b0), .pin4(1'b0), .pin5(1'b0), .pin6(1'b0),
    .pin7(1'b1), .pin8(1'b0), .pin9(1'b1), .pin10(_74161_4_pin15), .pin11(_74161_5_pin11),
    .pin12(_74161_5_pin12), .pin13(_74161_5_pin13), .pin14(_74161_5_pin14), .pin15(_74161_5_pin15),
    .pin16(1'b1));
  _74161 _74161_6 (
    .pin1(_7404_1_pin4), .pin2(_7404_1_pin6), .pin3(1'b0), .pin4(1'b0), .pin5(1'b0), .pin6(1'b0),
    .pin7(1'b1), .pin8(1'b0), .pin9(1'b1), .pin10(_74161_5_pin15), .pin13(_7421_1_pin13),
    .pin14(_74161_6_pin14), .pin16(1'b1));  // open: pin11, pin12, pin15
  _7411 _7411_1 (
    .pin1(_7411_1_pin1), .pin2(_74161_2_pin11), .pin3(_74161_2_pin12), .pin4(_7411_1_pin4),
    .pin5(_7411_1_pin5), .pin6(_7411_1_pin6), .pin7(1'b0), .pin8(_7411_1_pin8), .pin9(_7411_1_pin5),
    .pin10(_7411_1_pin10), .pin11(_74161_2_pin13), .pin12(_7411_1_pin12), .pin13(_7411_1_pin5), .pin14(1'b1));
  _7432 _7432_1 (
    .pin1(1'b0), .pin2(1'b0), .pin4(_7432_1_pin4), .pin5(_7432_1_pin5), .pin6(_7432_1_pin6), .pin7(1'b0),
    .pin8(_7432_1_pin8), .pin9(_7411_1_pin12), .pin10(_7432_1_pin10), .pin11(_7432_1_pin10),
    .pin12(_7411_1_pin8), .pin13(_7411_1_pin6), .pin14(1'b1));  // open: pin3
  _7421 _7421_2 (
    .pin1(_7411_1_pin5), .pin2(_74161_2_pin13), .pin4(_74161_2_pin12), .pin5(_74161_2_pin11),
    .pin6(_7432_1_pin5), .pin7(1'b0), .pin8(_7421_2_pin8), .pin9(_7421_2_pin9), .pin10(_7421_2_pin10),
    .pin12(_7421_2_pin12), .pin13(1'b1), .pin14(1'b1));  // open: pin3, pin11
  _7404 _7404_2 (
    .pin1(_74161_2_pin13), .pin2(_7411_1_pin4), .pin3(_74161_2_pin12), .pin4(_7411_1_pin1),
    .pin5(_74161_2_pin11), .pin6(_7411_1_pin10), .pin7(1'b0), .pin8(_7421_2_pin12), .pin9(_7404_2_pin9),
    .pin10(_7421_2_pin10), .pin11(_7432_1_pin6), .pin12(_7421_2_pin9), .pin13(_7432_1_pin8), .pin14(1'b1));
  // _74808 _74808_1: pin names not known; wires that end beside it: 1'b0, 1'b0, _7421_1_pin4, _74161_3_pin14, _7411_1_pin5, _7421_1_pin5, _7421_1_pin4, _7432_1_pin4, 1'b0, 1'b1, _7411_1_pin5, _7411_1_pin4, _74808_1_p13, _74808_1_p13, _7411_1_pin1, _74808_1_p16, _74808_1_p16, _7411_1_pin10, _7404_2_pin9
  _7458 _7458_1 (
    .pin1(_7458_1_pin1), .pin2(_7421_1_pin13), .pin3(1'b1), .pin4(_7458_1_pin4), .pin5(_74161_5_pin14),
    .pin6(_7458_1_pin1), .pin7(1'b0), .pin8(_7458_1_pin8), .pin9(_7458_1_pin4), .pin10(_7421_1_pin12),
    .pin11(_7421_1_pin10), .pin12(1'b1), .pin13(1'b1), .pin14(1'b1));
  _7455 _7455_1 (
    .pin1(_7458_1_pin4), .pin2(_7455_1_pin2), .pin3(_7455_1_pin3), .pin4(_7455_1_pin4), .pin7(1'b0),
    .pin8(_7455_1_pin8), .pin10(_7455_1_pin2), .pin11(_7458_1_pin4), .pin12(_7455_1_pin12), .pin13(1'b1),
    .pin14(1'b1));  // open: pin5, pin6, pin9
  _7404 _7404_3 (
    .pin1(_74161_4_pin13), .pin2(_7455_1_pin4), .pin3(_7421_1_pin10), .pin4(_7455_1_pin3),
    .pin5(_7421_1_pin12), .pin6(_7455_1_pin12), .pin7(1'b0), .pin8(_7455_1_pin2), .pin9(_74161_5_pin14),
    .pin10(_7404_3_pin10), .pin11(_7404_3_pin11), .pin12(_7404_3_pin12), .pin13(_7455_1_pin8), .pin14(1'b1));
  _7421 _7421_3 (
    .pin1(_74161_5_pin13), .pin2(_74161_5_pin12), .pin4(_74161_5_pin11), .pin5(_74161_6_pin14),
    .pin6(_7458_1_pin4), .pin7(1'b0), .pin8(_7421_3_pin8), .pin9(_7421_1_pin12), .pin10(_7455_1_pin3),
    .pin12(_74161_4_pin13), .pin13(_7455_1_pin2), .pin14(1'b1));  // open: pin3, pin11
  _7408 _7408_1 (
    .pin1(_7421_3_pin8), .pin2(_7458_1_pin4), .pin3(_7404_3_pin11), .pin4(1'b0), .pin5(1'b0), .pin7(1'b0),
    .pin8(_7408_1_pin8), .pin9(_7455_1_pin8), .pin10(_7408_1_pin10), .pin11(_7408_1_pin10),
    .pin12(_7408_1_pin12), .pin13(_7404_3_pin10), .pin14(1'b1));  // open: pin6
  not not_1 (_7408_1_pin12, _7458_1_pin8);
  not not_2 (not_2_out, _7432_1_pin8);
  not not_3 (not_3_out, _7404_3_pin11);
  Break #(.Cycles(1000000)) break_1 (.brk(_7432_1_pin8));
  Break #(.Cycles(1000000)) break_2 (.brk(_7432_1_pin6));
  Break #(.Cycles(1000000)) break_3 (.brk(_7421_2_pin8));
  Break #(.Cycles(1000000)) break_4 (.brk(_7404_2_pin9));
  Break #(.Cycles(1000000)) break_5 (.brk(_7404_3_pin12));
  Break #(.Cycles(1000000)) break_6 (.brk(_7404_3_pin11));
  Break #(.Cycles(1000000)) break_7 (.brk(_7408_1_pin8));
  Break #(.Cycles(1000000)) break_8 (.brk(_7458_1_pin8));
  or or_1 (or_1_out, not_2_out, _7432_1_pin6, _7404_2_pin9);
  or or_2 (or_2_out, _7458_1_pin8, _7404_3_pin12, not_3_out);
  VGA vga_1 (.R(1'b0), .G(1'b1), .B(1'b1), .H(or_1_out), .V(or_2_out), .C(pxl));

  // Notes on the sheet:
  //   pxl: Hz: 2147483647
  //   Frame completion pulse
  //   Horizontal character counter
  //   Pixel clock divider
  //   Line completion pulse
  //   Line counter
  //   Character pixel horizontal (0-7)
  //   Character index horizontal (0-99)
  //   3 lines below are also character
  //   pixel vertical
  //   Current line vertical (0-524)
  //   Shifting current line bus left 3 bits
  //   should also give current vertical
  //   character
  //   High in hSync (chars 82-93)
  //   High in hBackPorch (chars 94-99)
  //   High in hVis (chars 0-79)
  //   High in hFrontPorch (chars 80-81)
  //   High in vBackPorch (lines 492-524)
  //   High in vFrontPorch (lines 480-489)
  //   High in vSync (lines 490-491)
  //   High in vVis (lines 0-479)
  //   Horizontal timing pulse generator
  //   Vertical timing pulse generator
endmodule
