// Digital circuit text-mode-improved.dig as structural Verilog
module text_mode_improved (
  input  pxl
);

  wire _7411_1_pin5, _7411_1_pin6, _7411_1_pin12, CD4043B_nq, CD4043B_q, rs_ff_as_1_nq, rs_ff_as_1_q,
       rs_ff_as_2_nq, rs_ff_as_2_q, rs_ff_as_3_nq, rs_ff_as_3_q;
  wire [13:0] _7411_1_pin4, hcount__744060_out;

  Counter #(.Bits(14)) hcount__744060 (.en(1'b1), .C(pxl), .clr(_7411_1_pin12), .out(hcount__744060_out));  // open: ovf
  _7411 _7411_1 (
    .pin1(hcount__744060_out[8]), .pin2(hcount__744060_out[9]), .pin3(1'b1), .pin4(_7411_1_pin4[0]),
    .pin5(_7411_1_pin5), .pin6(_7411_1_pin6), .pin7(1'b0), .pin8(_7411_1_pin5), .pin9(_7411_1_pin4[2]),
    .pin10(_7411_1_pin4[3]), .pin11(_7411_1_pin4[9]), .pin12(_7411_1_pin12), .pin13(hcount__744060_out[5]),
    .pin14(1'b1));
  Counter #(.Bits(14)) vcount__744060 (
    .en(1'b1), .C(_7411_1_pin12), .clr(_7411_1_pin6), .out(_7411_1_pin4));  // open: ovf
  RS_FF_AS rs_ff_as_1 (.S(1'b0), .R(1'b0), .Q(rs_ff_as_1_q), .nQ(rs_ff_as_1_nq));
  RS_FF_AS rs_ff_as_2 (.S(1'b0), .R(1'b0), .Q(rs_ff_as_2_q), .nQ(rs_ff_as_2_nq));
  RS_FF_AS CD4043B (.S(_7411_1_pin12), .R(1'b0), .Q(CD4043B_q), .nQ(CD4043B_nq));
  RS_FF_AS rs_ff_as_3 (.S(_7411_1_pin6), .R(1'b0), .Q(rs_ff_as_3_q), .nQ(rs_ff_as_3_nq));
  Break vsync_low (.brk(rs_ff_as_1_nq));
  Break hsync_low (.brk(rs_ff_as_2_nq));
  Break hVis_low (.brk(CD4043B_nq));
  Break vVis_low (.brk(rs_ff_as_3_nq));
  Break vsync_high (.brk(rs_ff_as_1_q));
  Break hsync_high (.brk(rs_ff_as_2_q));
  Break hVis_high (.brk(CD4043B_q));
  Break vVis_high (.brk(rs_ff_as_3_q));
  VGA vga_1 (.R(1'b1), .G(1'b1), .B(1'b1), .H(rs_ff_as_2_q), .V(rs_ff_as_1_q), .C(pxl));

  // Notes on the sheet:
  //   pxl: Hz: 20
  //   vSync
  //   hSync
  //   hVis
  //   vVis
endmodule
